// Logisim project alarme-residencial.circ as structural Verilog
module comparador_4bits (
  input  in_1,
  input  in_2,
  input  in_3,
  input  in_4,
  input  in_5,
  input  in_6,
  input  in_7,
  input  in_8,
  output out_9
);

  wire and_1_out, and_2_out, xnor_1_out, xnor_2_out, xnor_3_out, xnor_4_out;

  xnor xnor_1 (xnor_1_out, in_1, in_2);
  xnor xnor_2 (xnor_2_out, in_3, in_4);
  xnor xnor_3 (xnor_3_out, in_5, in_6);
  xnor xnor_4 (xnor_4_out, in_7, in_8);
  and and_1 (and_1_out, xnor_1_out, xnor_2_out);
  and and_2 (and_2_out, xnor_3_out, xnor_4_out);
  and and_3 (out_9, and_1_out, and_2_out);
endmodule

module entrada_senha (
  output out_1
);

  wire button_1_out, button_2_out, button_3_out, button_4_out, button_5_out, button_6_out, button_7_out,
       button_8_out, comparador_4bits_1_out_9, comparador_4bits_2_out_9, comparador_4bits_3_out_9,
       comparador_4bits_4_out_9, contador_decadico_1_dig_0, contador_decadico_1_dig_1,
       contador_decadico_1_dig_2, contador_decadico_1_dig_3, contador_decadico_2_dig_0,
       contador_decadico_2_dig_1, contador_decadico_2_dig_2, contador_decadico_2_dig_3,
       contador_decadico_3_dig_0, contador_decadico_3_dig_1, contador_decadico_3_dig_2,
       contador_decadico_3_dig_3, contador_decadico_4_dig_0, contador_decadico_4_dig_1,
       contador_decadico_4_dig_2, contador_decadico_4_dig_3, contador_decadico_5_dig_0,
       contador_decadico_5_dig_1, contador_decadico_5_dig_2, contador_decadico_5_dig_3,
       contador_decadico_6_dig_0, contador_decadico_6_dig_1, contador_decadico_6_dig_2,
       contador_decadico_6_dig_3, contador_decadico_7_dig_0, contador_decadico_7_dig_1,
       contador_decadico_7_dig_2, contador_decadico_7_dig_3, contador_decadico_8_dig_0,
       contador_decadico_8_dig_1, contador_decadico_8_dig_2, contador_decadico_8_dig_3;

  Button button_1 (.out(button_1_out));
  contador_decadico contador_decadico_1 (
    .clock(button_1_out), .dig_3(contador_decadico_1_dig_3), .dig_2(contador_decadico_1_dig_2),
    .dig_1(contador_decadico_1_dig_1), .dig_0(contador_decadico_1_dig_0));
  Button button_2 (.out(button_2_out));
  contador_decadico contador_decadico_2 (
    .clock(button_2_out), .dig_3(contador_decadico_2_dig_3), .dig_2(contador_decadico_2_dig_2),
    .dig_1(contador_decadico_2_dig_1), .dig_0(contador_decadico_2_dig_0));
  contador_decadico contador_decadico_3 (
    .clock(button_3_out), .dig_3(contador_decadico_3_dig_3), .dig_2(contador_decadico_3_dig_2),
    .dig_1(contador_decadico_3_dig_1), .dig_0(contador_decadico_3_dig_0));
  Button button_3 (.out(button_3_out));
  comparador_4bits comparador_4bits_1 (
    .in_1(contador_decadico_1_dig_3), .in_2(contador_decadico_2_dig_3), .in_3(contador_decadico_1_dig_2),
    .in_4(contador_decadico_2_dig_2), .in_5(contador_decadico_1_dig_1), .in_6(contador_decadico_2_dig_1),
    .in_7(contador_decadico_1_dig_0), .in_8(contador_decadico_2_dig_0), .out_9(comparador_4bits_1_out_9));
  contador_decadico contador_decadico_4 (
    .clock(button_4_out), .dig_3(contador_decadico_4_dig_3), .dig_2(contador_decadico_4_dig_2),
    .dig_1(contador_decadico_4_dig_1), .dig_0(contador_decadico_4_dig_0));
  Button button_4 (.out(button_4_out));
  Button button_5 (.out(button_5_out));
  comparador_4bits comparador_4bits_2 (
    .in_1(contador_decadico_3_dig_3), .in_2(contador_decadico_4_dig_3), .in_3(contador_decadico_3_dig_2),
    .in_4(contador_decadico_4_dig_2), .in_5(contador_decadico_3_dig_1), .in_6(contador_decadico_4_dig_1),
    .in_7(contador_decadico_3_dig_0), .in_8(contador_decadico_4_dig_0), .out_9(comparador_4bits_2_out_9));
  contador_decadico contador_decadico_5 (
    .clock(button_5_out), .dig_3(contador_decadico_5_dig_3), .dig_2(contador_decadico_5_dig_2),
    .dig_1(contador_decadico_5_dig_1), .dig_0(contador_decadico_5_dig_0));
  Button button_6 (.out(button_6_out));
  contador_decadico contador_decadico_6 (
    .clock(button_6_out), .dig_3(contador_decadico_6_dig_3), .dig_2(contador_decadico_6_dig_2),
    .dig_1(contador_decadico_6_dig_1), .dig_0(contador_decadico_6_dig_0));
  contador_decadico contador_decadico_7 (
    .clock(button_7_out), .dig_3(contador_decadico_7_dig_3), .dig_2(contador_decadico_7_dig_2),
    .dig_1(contador_decadico_7_dig_1), .dig_0(contador_decadico_7_dig_0));
  Button button_7 (.out(button_7_out));
  comparador_4bits comparador_4bits_3 (
    .in_1(contador_decadico_5_dig_3), .in_2(contador_decadico_6_dig_3), .in_3(contador_decadico_5_dig_2),
    .in_4(contador_decadico_6_dig_2), .in_5(contador_decadico_5_dig_1), .in_6(contador_decadico_6_dig_1),
    .in_7(contador_decadico_5_dig_0), .in_8(contador_decadico_6_dig_0), .out_9(comparador_4bits_3_out_9));
  contador_decadico contador_decadico_8 (
    .clock(button_8_out), .dig_3(contador_decadico_8_dig_3), .dig_2(contador_decadico_8_dig_2),
    .dig_1(contador_decadico_8_dig_1), .dig_0(contador_decadico_8_dig_0));
  Button button_8 (.out(button_8_out));
  comparador_4bits comparador_4bits_4 (
    .in_1(contador_decadico_7_dig_3), .in_2(contador_decadico_8_dig_3), .in_3(contador_decadico_7_dig_2),
    .in_4(contador_decadico_8_dig_2), .in_5(contador_decadico_7_dig_1), .in_6(contador_decadico_8_dig_1),
    .in_7(contador_decadico_7_dig_0), .in_8(contador_decadico_8_dig_0), .out_9(comparador_4bits_4_out_9));
  and and_1 (out_1, comparador_4bits_4_out_9, comparador_4bits_3_out_9, comparador_4bits_2_out_9, comparador_4bits_1_out_9);
endmodule

module codificador_4bits (
  input  in_1,
  input  in_2,
  input  in_3,
  input  in_4,
  input  in_5,
  input  in_6,
  input  in_7,
  input  in_8,
  input  in_9,
  input  in_10,
  output out_11,
  output out_12,
  output out_13,
  output out_14
);

  wire or_1_out, or_2_out, or_3_out, or_4_out, or_5_out, or_6_out, or_7_out, or_11_out;

  or or_1 (or_1_out, in_6, in_5);
  or or_2 (or_2_out, in_4, in_3);
  or or_3 (or_3_out, in_8, in_7);
  or or_4 (or_4_out, in_4, in_3);
  or or_5 (or_5_out, in_9, in_7);
  or or_6 (or_6_out, in_5, in_3);
  or or_7 (or_7_out, in_1, in_1);
  or or_8 (out_11, in_2, in_1);
  or or_9 (out_12, or_1_out, or_2_out);
  or or_10 (out_13, or_3_out, or_4_out);
  or or_11 (or_11_out, or_5_out, or_6_out);
  or or_12 (out_14, or_11_out, or_7_out);
endmodule

module temporizador_3min (
  output out_1,
  output out_2,
  output out_3,
  output out_4,
  output out_5,
  output out_6,
  output out_7,
  output out_8,
  output out_9
);

  wire and_1_out, and_2_out, and_3_out, and_4_out, and_5_out, and_6_out, clock_1_out;

  Clock clock_1 (.out(clock_1_out));
  and and_1 (and_1_out, out_9, out_8, out_7);
  J_K_Flip_Flop #(.trigger("falling")) j_k_ff_1 (
    .J(and_1_out), .clk(clock_1_out), .K(and_1_out), .Q(out_6), .reset(and_3_out));  // open: Qn, preset, en
  and and_2 (and_2_out, out_9, out_8);
  J_K_Flip_Flop #(.trigger("falling")) j_k_ff_2 (
    .J(and_2_out), .clk(clock_1_out), .K(and_2_out), .Q(out_7), .reset(and_3_out));  // open: Qn, preset, en
  J_K_Flip_Flop #(.trigger("falling")) j_k_ff_3 (
    .J(out_9), .clk(clock_1_out), .K(out_9), .Q(out_8), .reset(and_3_out));  // open: Qn, preset, en
  and and_3 (and_3_out, out_6, out_8);
  J_K_Flip_Flop #(.trigger("falling")) j_k_ff_4 (
    .J(1'b1), .clk(clock_1_out), .K(1'b1), .Q(out_9), .reset(and_3_out));  // open: Qn, preset, en
  and and_4 (and_4_out, out_5, out_4);
  J_K_Flip_Flop #(.trigger("falling")) j_k_ff_5 (
    .J(and_4_out), .clk(and_3_out), .K(and_4_out), .Q(out_3), .reset(and_5_out));  // open: Qn, preset, en
  J_K_Flip_Flop #(.trigger("falling")) j_k_ff_6 (
    .J(out_5), .clk(and_3_out), .K(out_5), .Q(out_4), .reset(and_5_out));  // open: Qn, preset, en
  J_K_Flip_Flop #(.trigger("falling")) j_k_ff_7 (
    .J(1'b1), .clk(and_3_out), .K(1'b1), .Q(out_5), .reset(and_5_out));  // open: Qn, preset, en
  and and_5 (and_5_out, out_4, out_3);
  J_K_Flip_Flop #(.trigger("falling")) j_k_ff_8 (
    .J(out_2), .clk(and_5_out), .K(out_2), .Q(out_1), .reset(and_6_out));  // open: Qn, preset, en
  J_K_Flip_Flop #(.trigger("falling")) j_k_ff_9 (
    .J(1'b1), .clk(and_5_out), .K(1'b1), .Q(out_2), .reset(and_6_out));  // open: Qn, preset, en
  and and_6 (and_6_out, out_2, out_1);
endmodule

module contador_decadico (
  input  clock,
  output dig_3,
  output dig_2,
  output dig_1,
  output dig_0
);

  wire and_1_out, and_2_out, and_3_out;

  and and_1 (and_1_out, dig_0, dig_1, dig_2);
  J_K_Flip_Flop #(.trigger("falling")) j_k_ff_1 (
    .J(and_1_out), .clk(clock), .K(and_1_out), .Q(dig_3), .reset(and_3_out));  // open: Qn, preset, en
  and and_2 (and_2_out, dig_0, dig_1);
  J_K_Flip_Flop #(.trigger("falling")) j_k_ff_2 (
    .J(and_2_out), .clk(clock), .K(and_2_out), .Q(dig_2), .reset(and_3_out));  // open: Qn, preset, en
  J_K_Flip_Flop #(.trigger("falling")) j_k_ff_3 (
    .J(dig_0), .clk(clock), .K(dig_0), .Q(dig_1), .reset(and_3_out));  // open: Qn, preset, en
  J_K_Flip_Flop #(.trigger("falling")) j_k_ff_4 (
    .J(1'b1), .clk(clock), .K(1'b1), .Q(dig_0), .reset(and_3_out));  // open: Qn, preset, en
  and and_3 (and_3_out, dig_3, dig_1);
endmodule
